// Logisim project Лаишевкина_А.М._Лаб2.circ as structural Verilog: 4 circuits, main circuit main
module LL (
  input  q1,
  input  q2,
  input  q3,
  input  q4,
  output L1,
  output L2,
  output L3,
  output L4,
  output L5,
  output L6,
  output L7,
  output L8,
  output L9,
  output L10,
  output L11,
  output L12,
  output L13,
  output L14,
  output L15
);

  wire and_1_out, and_2_out, and_3_out, and_4_out, and_5_out, and_7_out, and_8_out, and_9_out, and_10_out,
       and_11_out, and_12_out, and_13_out, and_14_out, and_15_out, and_16_out, and_19_out, and_20_out,
       and_22_out, and_23_out, and_24_out, and_25_out, and_26_out, not_1_out, not_2_out, not_3_out,
       not_4_out, not_5_out, not_6_out, not_7_out, not_8_out, not_9_out, not_10_out, not_11_out, not_12_out,
       not_13_out, not_14_out, not_15_out, not_16_out, not_17_out, not_18_out, not_19_out, not_20_out,
       not_21_out, not_22_out, not_23_out, not_24_out, not_25_out, not_26_out, not_27_out, not_28_out,
       not_29_out, not_30_out, not_31_out, not_32_out, not_33_out, not_34_out, not_35_out, not_36_out,
       not_37_out, not_38_out, not_39_out, not_40_out, not_41_out, not_42_out, not_43_out, not_44_out,
       not_45_out;

  not not_1 (not_1_out, q1);
  not not_2 (not_2_out, q2);
  not not_3 (not_3_out, q3);
  not not_4 (not_4_out, q4);
  not not_5 (not_5_out, q1);
  not not_6 (not_6_out, q2);
  not not_7 (not_7_out, q3);
  not not_8 (not_8_out, q1);
  not not_9 (not_9_out, q2);
  not not_10 (not_10_out, q3);
  and and_1 (and_1_out, not_1_out, not_2_out, not_3_out);
  and and_2 (and_2_out, not_2_out, q3, not_4_out);
  and and_3 (and_3_out, q1, q2, not_3_out, not_4_out);
  and and_4 (and_4_out, not_5_out, q2, q3, q4);
  and and_5 (and_5_out, q1, not_6_out, not_7_out, q4);
  and and_6 (L11, not_8_out, not_9_out, not_10_out, q4);
  or or_1 (L1, and_1_out, and_2_out, and_3_out);
  or or_2 (L6, and_4_out, and_5_out);
  not not_11 (not_11_out, q1);
  not not_12 (not_12_out, q2);
  not not_13 (not_13_out, q3);
  not not_14 (not_14_out, q4);
  not not_15 (not_15_out, q2);
  not not_16 (not_16_out, q3);
  not not_17 (not_17_out, q4);
  not not_18 (not_18_out, q1);
  not not_19 (not_19_out, q2);
  not not_20 (not_20_out, q3);
  not not_21 (not_21_out, q4);
  and and_7 (and_7_out, not_11_out, not_13_out, not_14_out);
  and and_8 (and_8_out, not_11_out, not_12_out, q3, q4);
  and and_9 (and_9_out, q1, q3, not_14_out);
  and and_10 (and_10_out, q1, q2, not_13_out, q4);
  and and_11 (and_11_out, q1, not_15_out, q3, not_17_out);
  and and_12 (and_12_out, q1, q2, not_16_out);
  and and_13 (and_13_out, not_18_out, not_19_out, q3, not_21_out);
  and and_14 (and_14_out, q1, q2, not_20_out, not_21_out);
  or or_3 (L2, and_7_out, and_8_out, and_9_out, and_10_out);
  or or_4 (L7, and_11_out, and_12_out);
  or or_5 (L12, and_13_out, and_14_out);
  not not_22 (not_22_out, q1);
  not not_23 (not_23_out, q2);
  not not_24 (not_24_out, q3);
  not not_25 (not_25_out, q4);
  not not_26 (not_26_out, q2);
  not not_27 (not_27_out, q4);
  not not_28 (not_28_out, q1);
  not not_29 (not_29_out, q2);
  and and_15 (and_15_out, not_22_out, not_23_out, not_24_out, not_25_out);
  and and_16 (and_16_out, not_22_out, q2, not_24_out, q4);
  and and_17 (L8, q1, not_26_out, q3, not_27_out);
  and and_18 (L13, not_28_out, not_29_out, q3, q4);
  or or_6 (L3, and_15_out, and_16_out);
  not not_30 (not_30_out, q2);
  not not_31 (not_31_out, q1);
  not not_32 (not_32_out, q3);
  not not_33 (not_33_out, q4);
  not not_34 (not_34_out, q1);
  not not_35 (not_35_out, q2);
  not not_36 (not_36_out, q3);
  and and_19 (and_19_out, not_34_out, q2, q3, q4);
  and and_20 (and_20_out, q1, not_35_out, not_36_out);
  and and_21 (L9, q1, not_30_out, q3, q4);
  and and_22 (and_22_out, not_31_out, q2, not_32_out, not_33_out);
  and and_23 (and_23_out, q1, q2, not_32_out, q4);
  or or_7 (L4, and_19_out, and_20_out);
  or or_8 (L14, and_22_out, and_23_out);
  not not_37 (not_37_out, q1);
  not not_38 (not_38_out, q2);
  not not_39 (not_39_out, q3);
  not not_40 (not_40_out, q4);
  not not_41 (not_41_out, q2);
  not not_42 (not_42_out, q3);
  not not_43 (not_43_out, q4);
  not not_44 (not_44_out, q1);
  not not_45 (not_45_out, q3);
  and and_24 (and_24_out, q2, not_39_out);
  and and_25 (and_25_out, not_37_out, not_38_out, q4);
  and and_26 (and_26_out, not_37_out, q3, not_40_out);
  and and_27 (L5, q1, not_41_out, not_42_out, not_43_out);
  or or_9 (L10, and_24_out, and_25_out, and_26_out);
  and and_28 (L15, not_44_out, q2, not_45_out, q4);
endmodule

module QQ (
  input  q1,
  input  q2,
  input  q3,
  input  q4,
  input  x1,
  input  x2,
  input  pressed,
  output Q11,
  output Q22,
  output Q33,
  output Q44
);

  wire and_1_out, and_2_out, and_3_out, and_4_out, and_5_out, and_6_out, and_7_out, and_8_out, and_9_out,
       and_10_out, and_11_out, and_12_out, and_13_out, and_14_out, and_15_out, and_16_out, and_17_out,
       and_18_out, and_19_out, and_20_out, and_21_out, and_22_out, and_23_out, and_24_out, and_25_out,
       and_26_out, and_27_out, and_28_out, and_29_out, and_30_out, and_31_out, and_32_out, and_33_out,
       and_34_out, and_35_out, and_36_out, and_37_out, not_1_out, not_2_out, not_3_out, not_4_out, not_5_out,
       not_6_out, not_7_out, not_8_out, not_9_out, not_10_out, not_11_out, not_12_out, not_13_out,
       not_14_out, not_15_out, not_16_out, not_17_out, not_18_out, not_19_out, not_20_out, not_21_out,
       not_22_out, not_23_out, not_24_out, or_1_out, or_2_out, or_3_out, or_4_out;

  not not_1 (not_1_out, q1);
  not not_2 (not_2_out, q2);
  not not_3 (not_3_out, q3);
  not not_4 (not_4_out, q4);
  not not_5 (not_5_out, x1);
  not not_6 (not_6_out, x2);
  and and_1 (and_1_out, not_2_out, not_3_out, not_4_out, x1, not_6_out);
  and and_2 (and_2_out, q1, not_2_out, not_6_out);
  and and_3 (and_3_out, q1, q2, not_3_out);
  and and_4 (and_4_out, not_1_out, q2, q3, q4, not_5_out, not_6_out);
  and and_5 (and_5_out, q1, not_3_out, x1);
  and and_6 (and_6_out, q1, not_2_out, not_4_out, not_5_out);
  and and_7 (and_7_out, q1, not_2_out, q3, q4);
  Multiplexer multiplexer_1 (.in0(q1), .in1(or_1_out), .out(Q11), .sel(pressed));
  or or_1 (or_1_out, and_1_out, and_2_out, and_3_out, and_4_out, and_5_out, and_6_out, and_7_out);
  not not_7 (not_7_out, q1);
  not not_8 (not_8_out, q2);
  not not_9 (not_9_out, q3);
  not not_10 (not_10_out, q4);
  not not_11 (not_11_out, x1);
  not not_12 (not_12_out, x2);
  and and_8 (and_8_out, not_7_out, not_9_out, not_10_out, x2);
  and and_9 (and_9_out, q1, not_9_out, q4, not_11_out, x2);
  and and_10 (and_10_out, q1, not_8_out, q3, not_10_out, not_11_out, not_12_out);
  and and_11 (and_11_out, not_7_out, not_8_out, q3, q4, not_11_out, not_12_out);
  and and_12 (and_12_out, q2, not_9_out, not_10_out);
  and and_13 (and_13_out, q2, not_9_out, x1);
  and and_14 (and_14_out, not_7_out, q2, q4, not_11_out, x2);
  and and_15 (and_15_out, not_7_out, q2, q4, x1, not_12_out);
  Multiplexer multiplexer_2 (.in0(q2), .in1(or_2_out), .out(Q22), .sel(pressed));
  or or_2 (or_2_out, and_8_out, and_9_out, and_10_out, and_11_out, and_12_out, and_13_out, and_14_out, and_15_out);
  not not_13 (not_13_out, q1);
  not not_14 (not_14_out, q2);
  not not_15 (not_15_out, q3);
  not not_16 (not_16_out, q4);
  not not_17 (not_17_out, x1);
  not not_18 (not_18_out, x2);
  and and_16 (and_16_out, not_13_out, not_14_out, not_16_out, x2);
  and and_17 (and_17_out, not_13_out, not_14_out, not_16_out, x1);
  and and_18 (and_18_out, not_13_out, not_14_out, not_15_out, q4, not_17_out, not_18_out);
  and and_19 (and_19_out, q1, not_14_out, q4, not_17_out, x2);
  and and_20 (and_20_out, not_13_out, not_14_out, q3, not_16_out);
  and and_21 (and_21_out, not_14_out, q3, not_17_out, x2);
  and and_22 (and_22_out, not_14_out, q3, x1, not_18_out);
  and and_23 (and_23_out, q1, not_14_out, q3, q4);
  and and_24 (and_24_out, q1, q2, not_15_out, q4, not_17_out, not_18_out);
  and and_25 (and_25_out, not_13_out, q3, q4, not_17_out, x2);
  and and_26 (and_26_out, not_13_out, q3, q4, x1, not_18_out);
  and and_27 (and_27_out, not_13_out, not_14_out, q3, x2);
  Multiplexer multiplexer_3 (.in0(q3), .in1(or_3_out), .out(Q33), .sel(pressed));
  or or_3 (or_3_out, and_16_out, and_17_out, and_18_out, and_19_out, and_20_out, and_21_out, and_22_out, and_23_out, and_24_out, and_25_out, and_26_out, and_27_out);
  not not_19 (not_19_out, q1);
  not not_20 (not_20_out, q2);
  not not_21 (not_21_out, q3);
  not not_22 (not_22_out, q4);
  not not_23 (not_23_out, x1);
  not not_24 (not_24_out, x2);
  and and_28 (and_28_out, not_19_out, not_20_out, not_22_out, not_23_out, not_24_out);
  and and_29 (and_29_out, not_19_out, q4, not_23_out, x2);
  and and_30 (and_30_out, not_19_out, q4, x1, not_24_out);
  and and_31 (and_31_out, not_20_out, not_21_out, not_23_out, x2);
  and and_32 (and_32_out, not_21_out, q4, x1);
  and and_33 (and_33_out, q1, not_20_out, q3, not_22_out, x1, not_24_out);
  and and_34 (and_34_out, q1, not_20_out, q3, q4, not_23_out);
  and and_35 (and_35_out, not_20_out, q4, x2);
  and and_36 (and_36_out, q2, not_21_out, not_22_out, not_23_out, not_24_out);
  and and_37 (and_37_out, not_21_out, q4, x2);
  or or_4 (or_4_out, and_28_out, and_29_out, and_30_out, and_31_out, and_32_out, and_33_out, and_34_out, and_35_out, and_36_out, and_37_out);
  Multiplexer multiplexer_4 (.in0(q4), .in1(or_4_out), .out(Q44), .sel(pressed));
endmodule

module ii (
  input  q1,
  input  q2,
  input  q3,
  input  q4,
  input  x1,
  input  x2,
  output ii1,
  output ii2,
  output ii3
);

  wire and_1_out, and_2_out, and_3_out, and_4_out, and_5_out, not_1_out, not_2_out, not_3_out, not_4_out,
       not_5_out, not_6_out, not_7_out, not_8_out, not_9_out, not_10_out, not_11_out, not_12_out;

  not not_1 (not_1_out, q1);
  not not_2 (not_2_out, q2);
  not not_3 (not_3_out, q3);
  not not_4 (not_4_out, x1);
  and and_1 (and_1_out, q2, not_3_out, not_4_out, x2);
  and and_2 (and_2_out, not_1_out, not_2_out, q3, not_4_out, x2);
  and and_3 (and_3_out, not_1_out, not_3_out, q4, not_4_out, x2);
  or or_1 (ii1, and_1_out, and_2_out, and_3_out);
  not not_5 (not_5_out, q1);
  not not_6 (not_6_out, q2);
  not not_7 (not_7_out, q3);
  not not_8 (not_8_out, q4);
  not not_9 (not_9_out, x1);
  and and_4 (and_4_out, not_5_out, not_6_out, not_7_out, not_8_out, x2);
  and and_5 (and_5_out, not_5_out, q2, q3, q4, not_9_out, x2);
  or or_2 (ii2, and_4_out, and_5_out);
  not not_10 (not_10_out, q2);
  not not_11 (not_11_out, q4);
  not not_12 (not_12_out, x1);
  and and_6 (ii3, q1, not_10_out, q3, not_11_out, not_12_out, x2);
endmodule

module main (
);

  wire a, alarm, alarm_enabled, alarm_match, and_1_out, and_2_out, and_3_out, and_4_out, and_5_out,
       and_6_out, and_7_out, and_8_out, and_9_out, and_10_out, and_12_out, and_14_out, and_15_out,
       and_16_out, and_17_out, and_18_out, and_19_out, and_20_out, b, buzzer_1_p2, c, clear, clk, clr,
       comparator_1_eq, comparator_2_eq, comparator_3_eq, comparator_4_eq, comparator_5_eq, comparator_6_eq,
       counter_1_carry, counter_2_carry, counter_3_carry, counter_4_carry, counter_5_carry, counter_6_carry,
       counter_7_carry, counter_8_carry, counter_10_carry, counter_11_carry, counter_13_carry,
       counter_14_carry, d, d_ff_5_q, i1, i2, i3, k1, k2, k3, k4, k5, k6, k7, L1, L2, L3, L4, L5, L6, L7, L8,
       L9, L10, L11, L12, L13, L14, L15, multiplexer_10_out, not_1_out, not_2_out, not_3_out, not_4_out,
       not_5_out, not_6_out, not_7_out, not_8_out, not_9_out, not_10_out, not_11_out, not_12_out, not_13_out,
       not_14_out, not_15_out, or_1_out, or_2_out, or_7_out, or_8_out, or_9_out, or_11_out, or_12_out,
       or_13_out, or_14_out, or_15_out, or_16_out, or_17_out, pressed, Q1, q1_t, Q2, q2_t, Q3, q3_t, Q4,
       q4_t, ring, timed_ring, x1, x2;
  wire [1:0] adder_1_out, bit_extender_1_out, bit_extender_2_out, counter_14_q, counter_15_q, shifter_1_out;
  wire [2:0] counter_3_q, counter_4_q, counter_8_q, counter_9_q, counter_10_q;
  wire [3:0] bit_extender_3_out, bit_extender_8_out, bit_extender_10_out, counter_1_q, counter_2_q,
       counter_6_q, h_dec, h_dec_b, h_dec_c, h_ed, h_ed_b, h_ed_c, melody, min_dec, min_dec_b, min_dec_c,
       min_dec_t, min_ed, min_ed_b, min_ed_c, min_ed_t, multiplexer_1_out, multiplexer_2_out,
       multiplexer_3_out, multiplexer_4_out, multiplexer_5_out, multiplexer_6_out, multiplexer_7_out,
       multiplexer_8_out, multiplexer_9_out, sec_dec_c, sec_dec_t, sec_ed_c, sec_ed_t;
  wire [4:0] adder_2_out, bit_extender_4_out, bit_extender_5_out, bit_extender_16_out, bit_extender_17_out,
       h_whole, multiplier_1_out, multiplier_4_out;
  wire [5:0] adder_3_out, bit_extender_6_out, bit_extender_7_out, bit_extender_13_out, bit_extender_15_out,
       min_whole, multiplier_2_out, multiplier_3_out;
  wire [13:0] freq;

  Button reset (.out(clr));
  or or_1 (or_1_out, L7, L9);
  or or_2 (or_2_out, L9, L4);
  or or_3 (pressed, a, b, c, d);
  assign bit_extender_1_out = {{1{1'b0}}, or_1_out};  // Bit_Extender bit_extender_1
  assign bit_extender_2_out = {{1{1'b0}}, or_2_out};  // Bit_Extender bit_extender_2
  D_Flip_Flop #(.trigger("falling")) d_ff_1 (.D(Q1), .clk(clk), .Q(q1_t), .reset(clr));  // open: Qn, preset
  D_Flip_Flop #(.trigger("falling")) d_ff_2 (.D(Q2), .clk(clk), .Q(q2_t), .reset(clr));  // open: Qn, preset
  D_Flip_Flop #(.trigger("falling")) d_ff_3 (.D(Q3), .clk(clk), .Q(q3_t), .reset(clr));  // open: Qn, preset
  D_Flip_Flop #(.trigger("falling")) d_ff_4 (.D(Q4), .clk(clk), .Q(q4_t), .reset(clr));  // open: Qn, preset
  Shifter #(.width(2)) shifter_1 (.in(bit_extender_1_out), .\dist (1'b1), .out(shifter_1_out));
  Button u_a (.out(a));
  Hex_Digit_Display hex_digit_display_1 (.value(multiplexer_1_out));  // open: dp
  Multiplexer #(.width(4)) multiplexer_1 (.in0(h_dec_c), .in1(h_dec_b), .out(multiplexer_1_out), .sel(L7));
  Multiplexer #(.select(2), .width(4)) multiplexer_2 (
    .in0(4'b1010), .in1(4'b1011), .in2(4'b1100), .in3(melody), .out(multiplexer_2_out), .sel(adder_1_out));
  Adder #(.width(2)) adder_1 (.a(shifter_1_out), .b(bit_extender_2_out), .out(adder_1_out));  // open: cin, cout
  Button u_b (.out(b));
  Button u_c (.out(c));
  Hex_Digit_Display hex_digit_display_2 (.value(multiplexer_3_out));  // open: dp
  Multiplexer #(.width(4)) multiplexer_3 (.in0(h_ed_c), .in1(h_ed_b), .out(multiplexer_3_out), .sel(L7));
  Button u_d (.out(d));
  ROM #(.addrWidth(4), .dataWidth(7)) rom_1 (.addr(multiplexer_2_out), .data({k7, k6, k5, k4, k3, k2, k1}));
  or or_4 (x1, c, d);
  or or_5 (x2, b, d);
  Hex_Digit_Display hex_digit_display_3 (.value(multiplexer_4_out));  // open: dp
  Hex_Digit_Display hex_digit_display_4 (.value(multiplexer_5_out));  // open: dp
  Multiplexer #(.width(4)) multiplexer_4 (.in0(multiplexer_6_out), .in1(min_dec_b), .out(multiplexer_4_out), .sel(L7));
  Multiplexer #(.width(4)) multiplexer_5 (.in0(multiplexer_7_out), .in1(min_ed_b), .out(multiplexer_5_out), .sel(L7));
  Multiplexer #(.width(4)) multiplexer_6 (.in0(min_dec_c), .in1(min_dec_t), .out(multiplexer_6_out), .sel(L4));
  Multiplexer #(.width(4)) multiplexer_7 (.in0(min_ed_c), .in1(min_ed_t), .out(multiplexer_7_out), .sel(L4));
  Hex_Digit_Display hex_digit_display_5 (.value(multiplexer_8_out));  // open: dp
  Hex_Digit_Display hex_digit_display_6 (.value(multiplexer_9_out));  // open: dp
  Multiplexer #(.width(4)) multiplexer_8 (.in0(sec_dec_c), .in1(sec_dec_t), .out(multiplexer_8_out), .sel(L4));
  Multiplexer #(.width(4)) multiplexer_9 (.in0(sec_ed_c), .in1(sec_ed_t), .out(multiplexer_9_out), .sel(L4));
  LL ll_1 (
    .q1(q1_t), .q2(q2_t), .q3(q3_t), .q4(q4_t), .L1(L1), .L2(L2), .L3(L3), .L4(L4), .L5(L5), .L6(L6),
    .L7(L7), .L8(L8), .L9(L9), .L10(L10), .L11(L11), .L12(L12), .L13(L13), .L14(L14), .L15(L15));
  _7_Segment_Display u_7_segment_display_1 (.g(k1), .f(k2), .a(k7), .b(k6), .e(k3), .d(k4), .c(k5));  // open: dp
  _7_Segment_Display u_7_segment_display_2 (.g(k1), .f(k2), .a(k7), .b(k6), .e(k3), .d(k4), .c(k5));  // open: dp
  // Buzzer buzzer_1: pin names not known; wires that end beside it: freq, buzzer_1_p2
  or or_6 (buzzer_1_p2, ring, alarm);
  Clock clock_1 (.out(clk));
  QQ qq_1 (
    .q1(q1_t), .q2(q2_t), .q3(q3_t), .q4(q4_t), .x1(x1), .x2(x2), .pressed(pressed), .Q11(Q1), .Q22(Q2),
    .Q33(Q3), .Q44(Q4));
  ii ii_1 (.q1(q1_t), .q2(q2_t), .q3(q3_t), .q4(q4_t), .x1(x1), .x2(x2), .ii1(i1), .ii2(i2), .ii3(i3));
  not not_1 (not_1_out, L10);
  or or_7 (or_7_out, clr, i2);
  and and_1 (and_1_out, clk, L5);
  and and_2 (and_2_out, i1, L15);
  and and_3 (and_3_out, clk, not_1_out);
  Counter #(.max('h9), .width(4)) counter_1 (
    .clr(or_7_out), .clk(and_1_out), .carry(counter_1_carry), .Q(counter_1_q));  // open: load, up, count, D
  Counter #(.max('h9), .trigger("falling"), .width(4)) counter_2 (
    .clr(clr), .clk(or_8_out), .carry(counter_2_carry), .Q(counter_2_q));  // open: load, up, count, D
  or or_8 (or_8_out, and_2_out, and_3_out);
  assign sec_ed_t = L4 ? counter_1_q : 4'bz;  // Controlled_Buffer controlled_buffer_1
  and and_4 (and_4_out, L3, not_2_out);
  assign sec_ed_c = and_4_out ? counter_2_q : 4'bz;  // Controlled_Buffer controlled_buffer_2
  Counter #(.max('h5), .width(3)) counter_3 (
    .clr(or_7_out), .clk(counter_1_carry), .carry(counter_3_carry), .Q(counter_3_q));  // open: load, up, count, D
  not not_2 (not_2_out, L4);
  and and_5 (and_5_out, L14, i1, L7);
  Counter #(.max('h5), .trigger("falling"), .width(3)) counter_4 (
    .clr(clr), .clk(counter_2_carry), .carry(counter_4_carry), .Q(counter_4_q));  // open: load, up, count, D
  Counter #(.max('h9), .width(4)) counter_5 (
    .clr(or_11_out), .clk(and_5_out), .carry(counter_5_carry), .Q(min_ed_b));  // open: load, up, count, D
  assign bit_extender_3_out = {{1{1'b0}}, counter_3_q};  // Bit_Extender bit_extender_3
  assign sec_dec_t = L4 ? bit_extender_3_out : 4'bz;  // Controlled_Buffer controlled_buffer_3
  assign bit_extender_4_out = {{1{1'b0}}, h_ed_b};  // Bit_Extender bit_extender_4
  assign bit_extender_5_out = {{1{1'b0}}, h_dec_b};  // Bit_Extender bit_extender_5
  assign bit_extender_6_out = {{2{1'b0}}, min_ed_b};  // Bit_Extender bit_extender_6
  assign bit_extender_7_out = {{2{1'b0}}, min_dec_b};  // Bit_Extender bit_extender_7
  not not_3 (not_3_out, L15);
  and and_6 (and_6_out, not_3_out, counter_4_carry);
  assign bit_extender_8_out = {{1{1'b0}}, counter_4_q};  // Bit_Extender bit_extender_8
  Multiplier #(.width(5)) multiplier_1 (
    .a(5'b01010), .b(bit_extender_5_out), .out(multiplier_1_out));  // open: cin, cout
  Multiplier #(.width(6)) multiplier_2 (
    .a(6'b001010), .b(bit_extender_7_out), .out(multiplier_2_out));  // open: cin, cout
  Comparator #(.width(6)) comparator_1 (.a(min_whole), .b({6{1'b0}}), .eq(comparator_1_eq));  // open: gt, lt
  Comparator #(.width(6)) comparator_2 (.a(min_whole), .b(6'b001111), .eq(comparator_2_eq));  // open: gt, lt
  Comparator #(.width(6)) comparator_3 (.a(min_whole), .b(6'b011110), .eq(comparator_3_eq));  // open: gt, lt
  Comparator #(.width(6)) comparator_4 (.a(min_whole), .b(6'b101101), .eq(comparator_4_eq));  // open: gt, lt
  not not_4 (not_4_out, L7);
  and and_7 (and_7_out, not_4_out, i1, L14);
  and and_8 (and_8_out, L3, not_5_out);
  assign sec_dec_c = and_8_out ? bit_extender_8_out : 4'bz;  // Controlled_Buffer controlled_buffer_4
  not not_5 (not_5_out, L4);
  Counter #(.max('h9), .width(4)) counter_6 (
    .clr(or_7_out), .clk(counter_3_carry), .carry(counter_6_carry), .Q(counter_6_q));  // open: load, up, count, D
  Adder #(.width(5)) adder_2 (.a(bit_extender_4_out), .b(multiplier_1_out), .out(adder_2_out));  // open: cin, cout
  Adder #(.width(6)) adder_3 (.a(bit_extender_6_out), .b(multiplier_2_out), .out(adder_3_out));  // open: cin, cout
  Counter #(.max('h9), .trigger("falling"), .width(4)) counter_7 (
    .clr(clr), .clk(or_9_out), .carry(counter_7_carry), .Q(min_ed));  // open: load, up, count, D
  or or_9 (or_9_out, and_7_out, and_6_out);
  or or_10 (timed_ring, comparator_1_eq, comparator_2_eq, comparator_3_eq, comparator_4_eq);
  Counter #(.max('h5), .width(3)) counter_8 (
    .clr(or_11_out), .clk(counter_5_carry), .carry(counter_8_carry), .Q(counter_8_q));  // open: load, up, count, D
  assign min_ed_t = L4 ? counter_6_q : 4'bz;  // Controlled_Buffer controlled_buffer_5
  Comparator #(.width(5)) comparator_5 (.a(h_whole), .b(adder_2_out), .eq(comparator_5_eq));  // open: gt, lt
  Comparator #(.width(6)) comparator_6 (.a(adder_3_out), .b(min_whole), .eq(comparator_6_eq));  // open: gt, lt
  not not_6 (not_6_out, L14);
  and and_9 (and_9_out, not_6_out, counter_7_carry);
  and and_10 (and_10_out, L2, not_8_out);
  assign min_ed_c = and_10_out ? min_ed : 4'bz;  // Controlled_Buffer controlled_buffer_6
  and and_11 (alarm_match, comparator_5_eq, comparator_6_eq);
  D_Flip_Flop d_ff_5 (.D(timed_ring), .clk(clk), .Q(d_ff_5_q));  // open: Qn, preset, reset
  not not_7 (not_7_out, L7);
  and and_12 (and_12_out, not_7_out, i1, L13);
  not not_8 (not_8_out, L4);
  Counter #(.max('h5), .width(3)) counter_9 (
    .clr(or_7_out), .clk(counter_6_carry), .Q(counter_9_q));  // open: load, up, count, D, carry
  or or_11 (or_11_out, counter_8_carry, clr);
  assign min_dec_b = {{1{1'b0}}, counter_8_q};  // Bit_Extender bit_extender_9
  not not_9 (not_9_out, d_ff_5_q);
  Counter #(.max('h5), .trigger("falling"), .width(3)) counter_10 (
    .clr(clr), .clk(or_12_out), .carry(counter_10_carry), .Q(counter_10_q));  // open: load, up, count, D
  or or_12 (or_12_out, and_12_out, and_9_out);
  and and_13 (ring, timed_ring, not_9_out);
  assign bit_extender_10_out = {{1{1'b0}}, counter_9_q};  // Bit_Extender bit_extender_10
  assign min_dec_t = L4 ? bit_extender_10_out : 4'bz;  // Controlled_Buffer controlled_buffer_7
  not not_10 (not_10_out, alarm_enabled);
  D_Flip_Flop d_ff_6 (.D(multiplexer_10_out), .clk(clk), .Q(alarm_enabled));  // open: Qn, preset, reset
  Multiplexer multiplexer_10 (.in0(alarm_enabled), .in1(not_10_out), .out(multiplexer_10_out), .sel(i3));
  not not_11 (not_11_out, L13);
  and and_14 (and_14_out, not_11_out, counter_10_carry);
  assign min_dec = {{1{1'b0}}, counter_10_q};  // Bit_Extender bit_extender_11
  Counter #(.max('h9), .width(4)) counter_11 (
    .clr(or_17_out), .clk(and_15_out), .carry(counter_11_carry), .Q(h_ed_b));  // open: load, up, count, D
  and and_15 (and_15_out, L12, i1, L7);
  Counter #(.max('h9), .width(4)) counter_12 (.clk(and_16_out), .Q(melody));  // open: clr, load, up, count, D, carry
  and and_16 (and_16_out, i1, L9);
  not not_12 (not_12_out, L7);
  and and_17 (and_17_out, not_12_out, i1, L12);
  and and_18 (and_18_out, L2, not_13_out);
  assign min_dec_c = and_18_out ? min_dec : 4'bz;  // Controlled_Buffer controlled_buffer_8
  not not_13 (not_13_out, L4);
  or or_13 (or_13_out, clear, clr);
  Counter #(.max('h9), .trigger("falling"), .width(4)) counter_13 (
    .clr(or_13_out), .clk(or_14_out), .carry(counter_13_carry), .Q(h_ed));  // open: load, up, count, D
  or or_14 (or_14_out, and_17_out, and_14_out);
  ROM #(.addrWidth(4), .dataWidth(14)) rom_2 (.addr(melody), .data(freq));
  not not_14 (not_14_out, L12);
  and and_19 (and_19_out, not_14_out, counter_13_carry);
  Counter #(.max('h2), .width(2)) counter_14 (
    .clr(or_17_out), .clk(counter_11_carry), .carry(counter_14_carry), .Q(counter_14_q));  // open: load, up, count, D
  not not_15 (not_15_out, L7);
  and and_20 (and_20_out, not_15_out, i1, L11);
  assign h_ed_c = L1 ? h_ed : 4'bz;  // Controlled_Buffer controlled_buffer_9
  or or_15 (or_15_out, clear, clr);
  Counter #(.max('h2), .trigger("falling"), .width(2)) counter_15 (
    .clr(or_15_out), .clk(or_16_out), .Q(counter_15_q));  // open: load, up, count, D, carry
  or or_16 (or_16_out, and_20_out, and_19_out);
  or or_17 (or_17_out, counter_14_carry, clr);
  and and_21 (alarm, alarm_match, alarm_enabled);
  assign h_dec_b = {{2{1'b0}}, counter_14_q};  // Bit_Extender bit_extender_12
  assign bit_extender_13_out = {{2{1'b0}}, min_dec};  // Bit_Extender bit_extender_13
  assign h_dec = {{2{1'b0}}, counter_15_q};  // Bit_Extender bit_extender_14
  assign bit_extender_15_out = {{2{1'b0}}, min_ed};  // Bit_Extender bit_extender_15
  Multiplier #(.width(6)) multiplier_3 (
    .a(6'b001010), .b(bit_extender_13_out), .out(multiplier_3_out));  // open: cin, cout
  assign bit_extender_16_out = {{1{1'b0}}, h_ed};  // Bit_Extender bit_extender_16
  assign bit_extender_17_out = {{1{1'b0}}, h_dec};  // Bit_Extender bit_extender_17
  assign h_dec_c = L1 ? h_dec : 4'bz;  // Controlled_Buffer controlled_buffer_10
  Adder #(.width(6)) adder_4 (.a(bit_extender_15_out), .b(multiplier_3_out), .out(min_whole));  // open: cin, cout
  Multiplier #(.width(5)) multiplier_4 (
    .a(5'b01010), .b(bit_extender_17_out), .out(multiplier_4_out));  // open: cin, cout
  Adder #(.width(5)) adder_5 (.a(bit_extender_16_out), .b(multiplier_4_out), .out(h_whole));  // open: cin, cout
  Comparator #(.width(5)) comparator_7 (.a(5'b11000), .b(h_whole), .eq(clear));  // open: gt, lt

  // Notes on the sheet:
  //   contents of rom_1 (hex, n*v repeats v):
  //   7e 30 6d 79 33 5b 5f 70 7f 7b 37 4e 77
  //   contents of rom_2 (hex, n*v repeats v):
  //   12c 190 1f4 258 2bc 320 384 3e8 44c 4b0
endmodule
