// Logisim project Лаишевкина_А.М._lab2.circ as structural Verilog: 1 circuit, main circuit main
module main (
  input  [20:0] M,
  input  [7:0] in_2
);

  wire and_1_out, clock_1_out, or_1_out;
  wire [1:0] bit_extender_5_out;
  wire [6:0] adder_1_out;
  wire [7:0] adder_2_out, bit_extender_1_out, divider_1_rem, shifter_1_out;
  wire [7:7] adder_1_cout;
  wire [8:0] bit_extender_2_out, bit_extender_3_out, bit_extender_4_out, demultiplexer_1_out0,
       demultiplexer_1_out1, demultiplexer_1_out2, demultiplexer_1_out3;
  wire [8:8] adder_2_cout;

  Clock clock_1 (.out(clock_1_out));
  assign bit_extender_1_out = {{1{1'b0}}, M[6:0]};  // Bit_Extender bit_extender_1
  Adder #(.width(7)) adder_1 (.a(M[13:7]), .b(M[20:14]), .out(adder_1_out), .cout(adder_1_cout[7]));  // open: cin
  Divider divider_1 (.a(in_2), .b(8'h4), .rem(divider_1_rem));  // open: out, upper
  assign bit_extender_2_out = {{2{1'b0}}, M[20:14]};  // Bit_Extender bit_extender_2
  assign bit_extender_3_out = {{2{1'b0}}, M[13:7]};  // Bit_Extender bit_extender_3
  assign bit_extender_4_out = {{2{1'b0}}, M[6:0]};  // Bit_Extender bit_extender_4
  Bit_Extender #(.out_width(2)) bit_extender_5 (.in(divider_1_rem), .out(bit_extender_5_out));
  Shifter #(.shift("rl")) shifter_1 (.in({adder_1_cout[7], adder_1_out}), .\dist (3'b011), .out(shifter_1_out));
  Adder adder_2 (.a(bit_extender_1_out), .b(shifter_1_out), .out(adder_2_out), .cout(adder_2_cout[8]));  // open: cin
  and and_1 (and_1_out, bit_extender_5_out[0], bit_extender_5_out[1]);
  or or_1 (or_1_out, bit_extender_5_out[0], bit_extender_5_out[1]);
  Demultiplexer #(.select(2), .tristate("true"), .width(9)) demultiplexer_1 (
    .out0(demultiplexer_1_out0), .out1(demultiplexer_1_out1), .out2(demultiplexer_1_out2),
    .out3(demultiplexer_1_out3), .in({adder_2_cout[8], adder_2_out}), .sel(bit_extender_5_out));
  Demultiplexer #(.tristate("true"), .width(9)) demultiplexer_2 (
    .out0(demultiplexer_1_out3), .out1(demultiplexer_1_out2), .in(bit_extender_2_out), .sel(and_1_out));
  Demultiplexer #(.tristate("true"), .width(9)) demultiplexer_3 (
    .out0(demultiplexer_1_out2), .out1(demultiplexer_1_out1), .in(bit_extender_3_out),
    .sel(bit_extender_5_out[1]));
  Demultiplexer #(.tristate("true"), .width(9)) demultiplexer_4 (
    .out0(demultiplexer_1_out1), .out1(demultiplexer_1_out0), .in(bit_extender_4_out), .sel(or_1_out));
  RAM #(.dataWidth(9)) ram_1 (
    .addr(in_2), .we(clock_1_out), .clk(clock_1_out), .din(demultiplexer_1_out3));  // open: oe, dout
  RAM #(.dataWidth(9)) ram_2 (
    .addr(in_2), .we(clock_1_out), .clk(clock_1_out), .din(demultiplexer_1_out2));  // open: oe, dout
  RAM #(.dataWidth(9)) ram_3 (
    .addr(in_2), .we(clock_1_out), .clk(clock_1_out), .din(demultiplexer_1_out1));  // open: oe, dout
  RAM #(.dataWidth(9)) ram_4 (
    .addr(in_2), .we(clock_1_out), .clk(clock_1_out), .din(demultiplexer_1_out0));  // open: oe, dout

  // Notes on the sheet:
  //   M3
  //   M2
  //   M1
  //   R
  //   M1
  //   M2
  //   M3
endmodule
