// Logisim project Радионова_П.В._Лаб3.circ as structural Verilog: 2 circuits, main circuit main
module main (
  input  [8:0] in_1,
  input  RND,
  input  RST
);

  wire and_1_out, cache_memory_1_hit, cache_memory_2_hit, cache_memory_3_hit, cache_memory_4_hit,
       cache_memory_5_hit, cache_memory_6_hit, cache_memory_7_hit, cache_memory_8_hit, CLK_out,
       comparator_1_eq, decoder_1_out0, decoder_1_out1, decoder_1_out2, decoder_1_out3, decoder_1_out4,
       decoder_1_out5, decoder_1_out6, decoder_1_out7, not_1_out, or_1_out, undriven;
  wire [1:0] counter_1_q;
  wire [7:0] cache_memory_1_word, cache_memory_2_word, cache_memory_3_word, cache_memory_4_word,
       cache_memory_5_word, cache_memory_6_word, cache_memory_7_word, cache_memory_8_word, multiplexer_2_out;
  wire [8:0] multiplexer_1_out, random_1_out;
  wire [63:0] ram_1_dout;

  Clock CLK (.out(CLK_out));
  Random #(.width(9)) random_1 (.clr(undriven), .clk(RND), .out(random_1_out));  // open: next
  Multiplexer #(.width(9)) multiplexer_1 (.in0(in_1), .in1(random_1_out), .out(multiplexer_1_out), .sel(RND));
  Counter #(.max('h3), .width(2)) counter_1 (.Q(counter_1_q), .clk(CLK_out));  // open: load, D, count, carry, up, clr
  Comparator #(.width(2)) comparator_1 (.a(2'b00), .b(counter_1_q), .eq(comparator_1_eq));  // open: gt, lt
  RAM #(.addrWidth(6), .asyncread("true"), .dataWidth(64)) ram_1 (
    .addr(multiplexer_1_out[8:3]), .oe(1'b1), .clk(and_1_out), .dout(ram_1_dout));  // open: we, din
  Decoder #(.select(3)) decoder_1 (
    .out0(decoder_1_out0), .out1(decoder_1_out1), .out2(decoder_1_out2), .out3(decoder_1_out3),
    .out4(decoder_1_out4), .out5(decoder_1_out5), .out6(decoder_1_out6), .out7(decoder_1_out7),
    .sel(multiplexer_1_out[5:3]), .en(1'b1));
  and and_1 (and_1_out, comparator_1_eq, not_1_out);
  cache_memory cache_memory_1 (
    .D(ram_1_dout), .address(multiplexer_1_out), .CLK(decoder_1_out0), .Write_enable(and_1_out), .RST(RST),
    .Word(cache_memory_1_word), .hit(cache_memory_1_hit));
  cache_memory cache_memory_2 (
    .D(ram_1_dout), .address(multiplexer_1_out), .CLK(decoder_1_out1), .Write_enable(and_1_out), .RST(RST),
    .Word(cache_memory_2_word), .hit(cache_memory_2_hit));
  cache_memory cache_memory_3 (
    .D(ram_1_dout), .address(multiplexer_1_out), .CLK(decoder_1_out2), .Write_enable(and_1_out), .RST(RST),
    .Word(cache_memory_3_word), .hit(cache_memory_3_hit));
  cache_memory cache_memory_4 (
    .D(ram_1_dout), .address(multiplexer_1_out), .CLK(decoder_1_out3), .Write_enable(and_1_out), .RST(RST),
    .Word(cache_memory_4_word), .hit(cache_memory_4_hit));
  cache_memory cache_memory_5 (
    .D(ram_1_dout), .address(multiplexer_1_out), .CLK(decoder_1_out4), .Write_enable(and_1_out), .RST(RST),
    .Word(cache_memory_5_word), .hit(cache_memory_5_hit));
  cache_memory cache_memory_6 (
    .D(ram_1_dout), .address(multiplexer_1_out), .CLK(decoder_1_out5), .Write_enable(and_1_out), .RST(RST),
    .Word(cache_memory_6_word), .hit(cache_memory_6_hit));
  cache_memory cache_memory_7 (
    .D(ram_1_dout), .address(multiplexer_1_out), .CLK(decoder_1_out6), .Write_enable(and_1_out), .RST(RST),
    .Word(cache_memory_7_word), .hit(cache_memory_7_hit));
  cache_memory cache_memory_8 (
    .D(ram_1_dout), .address(multiplexer_1_out), .CLK(decoder_1_out7), .Write_enable(and_1_out), .RST(RST),
    .Word(cache_memory_8_word), .hit(cache_memory_8_hit));
  or or_1 (or_1_out, cache_memory_1_hit, cache_memory_2_hit, cache_memory_3_hit, cache_memory_4_hit, cache_memory_5_hit, cache_memory_6_hit, cache_memory_7_hit, cache_memory_8_hit);
  not not_1 (not_1_out, or_1_out);
  Multiplexer #(.select(3), .width(8)) multiplexer_2 (
    .in0(cache_memory_1_word), .in1(cache_memory_2_word), .in2(cache_memory_3_word),
    .in3(cache_memory_4_word), .in4(cache_memory_5_word), .in5(cache_memory_6_word),
    .in6(cache_memory_7_word), .in7(cache_memory_8_word), .out(multiplexer_2_out),
    .sel(multiplexer_1_out[5:3]));
  Register #(.trigger("high")) register_1 (
    .D(multiplexer_2_out), .en(or_1_out), .clk(comparator_1_eq), .clr(RST));  // open: Q

  // Notes on the sheet:
  //   Адрес
  //   Случайный адрес
  //   Индекс
  //   Результат
endmodule

module cache_memory (
  input  [63:0] D,
  input  [8:0] address,
  input  CLK,
  input  Write_enable,
  input  RST,
  output [7:0] Word,
  output hit
);

  wire and_1_out, comparator_1_eq, register_1_q;
  wire [2:0] register_2_q;
  wire [63:0] register_3_q;

  and and_1 (and_1_out, CLK, Write_enable);
  Register #(.trigger("high"), .width(1)) register_1 (
    .D(1'b1), .en(Write_enable), .clk(CLK), .Q(register_1_q), .clr(RST));
  Register #(.trigger("high"), .width(3)) register_2 (
    .D(address[8:6]), .en(Write_enable), .clk(CLK), .Q(register_2_q), .clr(RST));
  Comparator #(.width(3)) comparator_1 (.a(address[8:6]), .b(register_2_q), .eq(comparator_1_eq));  // open: gt, lt
  Register #(.trigger("high"), .width(64)) register_3 (
    .D(D), .en(Write_enable), .clk(and_1_out), .Q(register_3_q), .clr(RST));
  Multiplexer #(.select(3), .width(8)) multiplexer_1 (
    .in0(register_3_q[7:0]), .in1(register_3_q[15:8]), .in2(register_3_q[23:16]), .in3(register_3_q[31:24]),
    .in4(register_3_q[39:32]), .in5(register_3_q[47:40]), .in6(register_3_q[55:48]),
    .in7(register_3_q[63:56]), .out(Word), .sel(address[2:0]));
  and and_2 (hit, comparator_1_eq, register_1_q, CLK);

  // Notes on the sheet:
  //   смещение
  //   Тэг
  //   Бит валидности
  //   тэг хранящейся строки
endmodule
