// Logisim project Радионова_П.В_Лаб2.circ as structural Verilog: 1 circuit, main circuit main
module main (
  input  [19:0] in_1,
  input  [7:0] \Адрес 
);

  wire adder_1_cout, adder_2_cout, and_1_out, and_2_out, and_3_out, clock_1_out, not_1_out, not_2_out,
       not_3_out, not_4_out, or_1_out, or_2_out, or_3_out;
  wire [2:0] bit_extender_1_out;
  wire [4:0] adder_1_out, xor_1_out;
  wire [5:0] adder_2_out, bit_extender_2_out, bit_extender_3_out;
  wire [6:0] bit_extender_4_out, bit_extender_5_out, bit_extender_6_out, bit_extender_7_out,
       bit_extender_8_out, demultiplexer_1_out0, demultiplexer_1_out1, demultiplexer_1_out2,
       demultiplexer_1_out3, demultiplexer_1_out4;
  wire [7:0] divider_1_rem;

  Clock clock_1 (.out(clock_1_out));
  assign xor_1_out = in_1[4:0] ^ in_1[9:5];  // XOR_Gate xor_1, 5 bits wide
  Divider divider_1 (.a(\Адрес ), .b(8'h5), .rem(divider_1_rem));  // open: out, upper
  Bit_Extender #(.out_width(3)) bit_extender_1 (.in(divider_1_rem), .out(bit_extender_1_out));
  not not_1 (not_1_out, bit_extender_1_out[0]);
  Adder #(.width(5)) adder_1 (.a(xor_1_out), .b(in_1[14:10]), .out(adder_1_out), .cout(adder_1_cout));  // open: cin
  not not_2 (not_2_out, bit_extender_1_out[0]);
  not not_3 (not_3_out, bit_extender_1_out[1]);
  and and_1 (and_1_out, bit_extender_1_out[0], bit_extender_1_out[1], not_4_out);
  not not_4 (not_4_out, bit_extender_1_out[2]);
  or or_1 (or_1_out, bit_extender_1_out[0], bit_extender_1_out[1], bit_extender_1_out[2]);
  or or_2 (or_2_out, not_1_out, bit_extender_1_out[1], bit_extender_1_out[2]);
  assign bit_extender_2_out = {{1{adder_1_cout}}, adder_1_out};  // Bit_Extender bit_extender_2
  assign bit_extender_3_out = {{1{1'b0}}, in_1[19:15]};  // Bit_Extender bit_extender_3
  and and_2 (and_2_out, not_2_out, not_3_out, bit_extender_1_out[2]);
  Adder #(.width(6)) adder_2 (
    .a(bit_extender_2_out), .b(bit_extender_3_out), .out(adder_2_out), .cout(adder_2_cout));  // open: cin
  or or_3 (or_3_out, and_2_out, and_1_out);
  and and_3 (and_3_out, or_1_out, or_2_out);
  assign bit_extender_4_out = {{1{adder_2_cout}}, adder_2_out};  // Bit_Extender bit_extender_4
  Demultiplexer #(.select(3), .tristate("true"), .width(7)) demultiplexer_1 (
    .out0(demultiplexer_1_out0), .out1(demultiplexer_1_out1), .out2(demultiplexer_1_out2),
    .out3(demultiplexer_1_out3), .out4(demultiplexer_1_out4), .in(bit_extender_4_out),
    .sel(bit_extender_1_out));  // open: out5, out6, out7
  assign bit_extender_5_out = {{2{1'b0}}, in_1[19:15]};  // Bit_Extender bit_extender_5
  Demultiplexer #(.tristate("true"), .width(7)) demultiplexer_2 (
    .out0(demultiplexer_1_out4), .out1(demultiplexer_1_out3), .in(bit_extender_5_out), .sel(and_2_out));
  assign bit_extender_6_out = {{2{1'b0}}, in_1[14:10]};  // Bit_Extender bit_extender_6
  Demultiplexer #(.tristate("true"), .width(7)) demultiplexer_3 (
    .out0(demultiplexer_1_out3), .out1(demultiplexer_1_out2), .in(bit_extender_6_out), .sel(or_3_out));
  assign bit_extender_7_out = {{2{1'b0}}, in_1[4:0]};  // Bit_Extender bit_extender_7
  Demultiplexer #(.tristate("true"), .width(7)) demultiplexer_4 (
    .out0(demultiplexer_1_out1), .out1(demultiplexer_1_out0), .in(bit_extender_7_out), .sel(or_1_out));
  assign bit_extender_8_out = {{2{1'b0}}, in_1[9:5]};  // Bit_Extender bit_extender_8
  Demultiplexer #(.tristate("true"), .width(7)) demultiplexer_5 (
    .out0(demultiplexer_1_out2), .out1(demultiplexer_1_out1), .in(bit_extender_8_out), .sel(and_3_out));
  RAM #(.dataWidth(7)) ram_1 (
    .addr(\Адрес ), .we(clock_1_out), .clk(clock_1_out), .din(demultiplexer_1_out4));  // open: oe, dout
  RAM #(.dataWidth(7)) ram_2 (
    .addr(\Адрес ), .we(clock_1_out), .clk(clock_1_out), .din(demultiplexer_1_out3));  // open: oe, dout
  RAM #(.dataWidth(7)) ram_3 (
    .addr(\Адрес ), .we(clock_1_out), .clk(clock_1_out), .din(demultiplexer_1_out2));  // open: oe, dout
  RAM #(.dataWidth(7)) ram_4 (
    .addr(\Адрес ), .we(clock_1_out), .clk(clock_1_out), .din(demultiplexer_1_out1));  // open: oe, dout
  RAM #(.dataWidth(7)) ram_5 (
    .addr(\Адрес ), .we(clock_1_out), .clk(clock_1_out), .din(demultiplexer_1_out0));  // open: oe, dout

  // Notes on the sheet:
  //   Сообщение
  //   Такт
  //   M4
  //   M3
  //   М2
  //   М1
  //   M1
  //   M2
  //   M3
  //   M4
  //   R
  //   1
  //   2
  //   3
  //   4
  //   5
endmodule
